// Logisim project JK-Flipflop.circ as structural Verilog: 1 circuit, main circuit main
module main (
  output [3:0] out_1
);

  wire and_1_out, and_2_out, and_3_out, and_4_out, clock_1_out, j_k_ff_1_qn, j_k_ff_2_qn, j_k_ff_3_qn,
       or_1_out;

  Clock clock_1 (.out(clock_1_out));
  J_K_Flip_Flop j_k_ff_1 (
    .J(and_3_out), .clk(clock_1_out), .K(or_1_out), .Q(out_1[2]), .Qn(j_k_ff_1_qn));  // open: preset, en, reset
  and and_1 (and_1_out, out_1[2], out_1[0]);
  or or_1 (or_1_out, j_k_ff_2_qn, out_1[0]);
  and and_2 (and_2_out, j_k_ff_1_qn, out_1[0]);
  J_K_Flip_Flop j_k_ff_2 (
    .J(and_2_out), .clk(clock_1_out), .K(and_1_out), .Q(out_1[1]), .Qn(j_k_ff_2_qn));  // open: preset, en, reset
  and and_3 (and_3_out, out_1[1], j_k_ff_3_qn);
  and and_4 (and_4_out, out_1[1], j_k_ff_1_qn);
  Hex_Digit_Display hex_digit_display_1 (.value({1'b0, out_1[2:0]}));  // open: dp
  J_K_Flip_Flop j_k_ff_3 (
    .J(1'b1), .clk(clock_1_out), .K(and_4_out), .Q(out_1[0]), .Qn(j_k_ff_3_qn));  // open: preset, en, reset

  assign out_1[3] = 1'b0;

  // Notes on the sheet:
  //   C
  //   B
  //   A
endmodule
