// Logisim project finalExam.circ as structural Verilog: 1 circuit, main circuit main
module main (
  output [3:0] out_1
);

  wire and_1_out, and_2_out, and_3_out, and_4_out, and_5_out, and_6_out, CLEAR_out, clock_1_out, not_1_out,
       not_2_out, not_3_out, not_4_out, not_5_out, not_6_out, not_7_out, not_8_out, or_1_out, or_2_out,
       or_3_out;

  Clock clock_1 (.out(clock_1_out));
  Button CLEAR (.out(CLEAR_out));
  and and_1 (and_1_out, out_1[0], not_1_out);
  or or_1 (or_1_out, and_1_out, and_2_out, and_3_out);
  and and_2 (and_2_out, not_2_out, out_1[2]);
  not not_1 (not_1_out, out_1[2]);
  not not_2 (not_2_out, out_1[0]);
  D_Flip_Flop C (.clk(clock_1_out), .D(or_1_out), .Q(out_1[2]), .reset(CLEAR_out));  // open: Qn, preset, en
  and and_3 (and_3_out, not_3_out, out_1[2]);
  not not_3 (not_3_out, out_1[1]);
  or or_2 (or_2_out, not_5_out, not_4_out);
  not not_4 (not_4_out, out_1[1]);
  not not_5 (not_5_out, out_1[0]);
  D_Flip_Flop B (.clk(clock_1_out), .D(or_2_out), .Q(out_1[1]), .reset(CLEAR_out));  // open: Qn, preset, en
  and and_4 (and_4_out, not_6_out, out_1[1]);
  not not_6 (not_6_out, out_1[0]);
  or or_3 (or_3_out, and_4_out, and_5_out, and_6_out);
  and and_5 (and_5_out, out_1[0], not_7_out);
  not not_7 (not_7_out, out_1[1]);
  D_Flip_Flop A (.clk(clock_1_out), .D(or_3_out), .Q(out_1[0]), .reset(CLEAR_out));  // open: Qn, preset, en
  and and_6 (and_6_out, not_8_out, out_1[2]);
  not not_8 (not_8_out, out_1[1]);
  Hex_Digit_Display hex_digit_display_1 (.value({1'b0, out_1[2:0]}));  // open: dp

  assign out_1[3] = 1'b0;
endmodule
