// Logisim project lab3A.circ as structural Verilog: 1 circuit, main circuit main
module main (
  input  A,
  input  B,
  input  C,
  input  D,
  input  A_2,
  input  B_2,
  input  C_2,
  input  D_2,
  input  A_3,
  input  B_3,
  input  C_3,
  input  D_3
);

  wire AND_2_out, AND_3_out, AND_4_out, AND_5_out, AND_6_out, AND_7_out, AND_out, not_1_out, not_2_out,
       not_3_out, not_4_out, not_5_out, not_6_out, not_7_out, not_8_out, not_9_out, not_10_out, not_11_out,
       not_12_out, OR_3_out, OR_5_out, OR_6_out, OR_out;

  not not_1 (not_1_out, A);
  not not_2 (not_2_out, A);
  not not_3 (not_3_out, B);
  not not_4 (not_4_out, B);
  not not_5 (not_5_out, C_2);
  not not_6 (not_6_out, A_2);
  not not_7 (not_7_out, D_2);
  not not_8 (not_8_out, B_2);
  not not_9 (not_9_out, C_3);
  not not_10 (not_10_out, C_3);
  not not_11 (not_11_out, D_3);
  not not_12 (not_12_out, D_3);
  and AND (AND_out, not_1_out, C);
  and AND_2 (AND_2_out, not_2_out, not_3_out, D);
  and AND_3 (AND_3_out, not_4_out, C, D);
  or OR (OR_out, A_2, not_5_out);
  or OR_2 (OR_out, not_6_out, C_2);
  or OR_3 (OR_3_out, B_2, not_7_out);
  or OR_4 (OR_3_out, not_8_out, D_2);
  and AND_4 (AND_4_out, A_3, not_9_out);
  and AND_5 (AND_5_out, B_3, not_10_out, not_11_out);
  and AND_6 (AND_6_out, A_3, B_3, not_12_out);
  or OR_5 (OR_5_out, AND_out, AND_2_out, AND_3_out);
  or OR_6 (OR_6_out, AND_4_out, AND_5_out, AND_6_out);
  LED led_1 (.in(OR_5_out));
  and AND_7 (AND_7_out, OR_out, OR_out, OR_3_out, OR_3_out);
  LED led_2 (.in(AND_7_out));
  LED led_3 (.in(OR_6_out));

  // Notes on the sheet:
  //   Output L:
  //   Output E
  //   Ouput G
  //   (SOP) L = A'C+A'B'D + B'CD 
  //   (POS) L = (C+D)(B'+C)(A'+C)(A'+D)(A'+B')
  //   (SOP) E = A'B'C'D'+A'BC'D+AB'CD'+ABCD
  //   (POS) E = (B+D')(A+C')(B'+D)(A'+C)
  //   (SOP) G = AC'+BC'D'+ABD'
  //   (POS) G = (A+B)(A+D')(A+C')(B+C')(C'+D')
endmodule
