// Logisim project lab3B.circ as structural Verilog: 1 circuit, main circuit main
module main (
  input  Cl,
  input  A,
  input  B
);

  wire m1_out, m2_out, m3_out, m4_out, m5_out, m6_out, m7_out, not_1_out, not_2_out, not_3_out, or_1_out,
       or_2_out;

  not not_1 (not_1_out, A);
  not not_2 (not_2_out, B);
  not not_3 (not_3_out, Cl);
  and m7 (m7_out, Cl, A, B);
  and m6 (m6_out, Cl, A, not_2_out);
  and m5 (m5_out, Cl, not_1_out, B);
  and m4 (m4_out, Cl, not_1_out, not_2_out);
  and m3 (m3_out, not_3_out, A, B);
  and m2 (m2_out, not_3_out, A, not_2_out);
  and m1 (m1_out, not_3_out, not_1_out, B);
  // AND_Gate m0 has open pins: in0=not_1_out, in1=not_3_out, in2=not_2_out, out=open
  or or_1 (or_1_out, m7_out, m6_out, m5_out, m3_out);
  or or_2 (or_2_out, m7_out, m4_out, m2_out, m1_out);
  LED led_1 (.in(or_1_out));
  LED led_2 (.in(or_2_out));

  // Notes on the sheet:
  //   CO
  //   S
  //   3x8 Line Decoder
  //   m7 - ABC
  //   m6 - ABC'
  //   m5 - AB'C
  //   m3 - A'BC
  //   m7 - ABC
  //   m4 - AB'C'
  //   m2 - A'BC'
  //   m1 - A'B'C
  //   CO
  //   S
endmodule
