// Logisim project paper.scissor.rock.N.circ as structural Verilog: 1 circuit, main circuit main
module main (
  input  A,
  input  B,
  input  C,
  input  D,
  input  A_2,
  input  B_2,
  input  C_2,
  input  D_2,
  input  A_3,
  input  B_3,
  input  C_3,
  input  D_3
);

  wire AND_2_out, AND_3_out, AND_out, not_1_out, not_2_out, not_3_out, not_4_out, not_5_out, not_6_out,
       not_7_out, not_8_out, OR_2_out, OR_3_out, OR_6_out, OR_out;

  or OR (OR_out, A, B);
  or OR_2 (OR_2_out, C, D);
  and AND (AND_out, OR_out, OR_2_out);
  or OR_3 (OR_3_out, A_2, B_2);
  or OR_4 (OR_3_out, A_2, D_2);
  or OR_5 (OR_3_out, C_2, D_2);
  not not_1 (not_1_out, C_2);
  not not_2 (not_2_out, D_2);
  not not_3 (not_3_out, A_2);
  not not_4 (not_4_out, B_2);
  or OR_6 (OR_6_out, A_3, B_3);
  or OR_7 (OR_6_out, B_3, C_3);
  or OR_8 (OR_6_out, C_3, D_3);
  not not_5 (not_5_out, C_3);
  not not_6 (not_6_out, D_3);
  not not_7 (not_7_out, A_3);
  not not_8 (not_8_out, B_3);
  LED N (.in(AND_out));
  or OR_9 (OR_3_out, B_2, not_1_out, not_2_out);
  or OR_10 (OR_3_out, not_3_out, not_4_out, C_2);
  or OR_11 (OR_6_out, A_3, not_5_out, not_6_out);
  or OR_12 (OR_6_out, not_7_out, not_8_out, D_3);
  buf AND_2 (AND_2_out, OR_3_out);  // AND_Gate
  buf AND_3 (AND_3_out, OR_6_out);  // AND_Gate
  LED N_2 (.in(AND_2_out));
  LED N_3 (.in(AND_3_out));

  // Notes on the sheet:
  //   C_2: pull=up
  //   C_3: pull=up
  //   C: pull=up
  //   Ouput N
  //   Ouput P1
  //   Ouput P2
  //   logic equation: N= BD + BC + AD + AC (SOP)
  //   N = (A+B)(C+D)  (POS)
  //   logic equation: P1 = A'BD + BCD + ACD' + AB'C'D (SOP)
  //   logic equation P2 = BC'D+AB'C+ACD+A'BCD'  (SOP)
  //   P1 = (A+B)(A+D)(C+D)(B+C'+D')(A'+B'+C)
  //   P2 = (A+B)(B+C)(C+D)(A+C'+D')(A'+B'+D) (POS)
endmodule
