// Logisim project project1.circ as structural Verilog: 2 circuits, main circuit 1b ALU
module _1b_ALU (
  input  C_in,
  input  [1:0] in_2,
  input  A,
  input  A_invert,
  input  B,
  input  B_invert,
  input  Less,
  output Result,
  output Set,
  output Overflow,
  output C_out
);

  wire and_1_out, or_1_out, xor_1_out, xor_2_out;

  xor xor_1 (xor_1_out, A, A_invert);
  xor xor_2 (xor_2_out, B, B_invert);
  and and_1 (and_1_out, xor_1_out, xor_2_out);
  or or_1 (or_1_out, xor_1_out, xor_2_out);
  Adder #(.width(1)) adder_1 (.a(xor_1_out), .b(xor_2_out), .out(Set), .cin(C_in), .cout(C_out));
  xor xor_3 (Overflow, C_in, C_out);
  Multiplexer #(.select(2)) multiplexer_1 (
    .in0(and_1_out), .in1(or_1_out), .in2(Set), .in3(Less), .out(Result), .sel(in_2));  // open: en
endmodule

module ALU (
  input  [3:0] in_1,
  input  [7:0] in_2,
  input  [7:0] in_3,
  output [7:0] out_4,
  output Zero,
  output Overflow
);

  wire n1b_alu_1_c_out, n1b_alu_2_c_out, n1b_alu_3_c_out, n1b_alu_4_c_out, n1b_alu_5_c_out, n1b_alu_6_c_out,
       n1b_alu_7_c_out, n1b_alu_8_set, xor_1_out;

  Hex_Digit_Display hex_digit_display_1 (.value(in_2[3:0]));  // open: dp
  Hex_Digit_Display hex_digit_display_2 (.value(in_2[7:4]));  // open: dp
  Hex_Digit_Display hex_digit_display_3 (.value(in_3[7:4]));  // open: dp
  Hex_Digit_Display hex_digit_display_4 (.value(in_3[3:0]));  // open: dp
  Hex_Digit_Display hex_digit_display_5 (.value(in_1));  // open: dp
  _1b_ALU u_1b_alu_1 (
    .A(in_3[0]), .B(in_2[0]), .Less(xor_1_out), .Result(out_4[0]), .C_in(in_1[2]), .in_2(in_1[1:0]),
    .C_out(n1b_alu_1_c_out), .B_invert(in_1[2]), .A_invert(in_1[3]));  // open: Set, Overflow
  _1b_ALU u_1b_alu_2 (
    .A(in_3[1]), .B(in_2[1]), .Less(1'b0), .Result(out_4[1]), .C_in(n1b_alu_1_c_out), .in_2(in_1[1:0]),
    .C_out(n1b_alu_2_c_out), .B_invert(in_1[2]), .A_invert(in_1[3]));  // open: Set, Overflow
  _1b_ALU u_1b_alu_3 (
    .A(in_3[2]), .B(in_2[2]), .Less(1'b0), .Result(out_4[2]), .C_in(n1b_alu_2_c_out), .in_2(in_1[1:0]),
    .C_out(n1b_alu_3_c_out), .B_invert(in_1[2]), .A_invert(in_1[3]));  // open: Set, Overflow
  _1b_ALU u_1b_alu_4 (
    .A(in_3[3]), .B(in_2[3]), .Less(1'b0), .Result(out_4[3]), .C_in(n1b_alu_3_c_out), .in_2(in_1[1:0]),
    .C_out(n1b_alu_4_c_out), .B_invert(in_1[2]), .A_invert(in_1[3]));  // open: Set, Overflow
  _1b_ALU u_1b_alu_5 (
    .A(in_3[4]), .B(in_2[4]), .Less(1'b0), .Result(out_4[4]), .C_in(n1b_alu_4_c_out), .in_2(in_1[1:0]),
    .C_out(n1b_alu_5_c_out), .B_invert(in_1[2]), .A_invert(in_1[3]));  // open: Set, Overflow
  _1b_ALU u_1b_alu_6 (
    .A(in_3[5]), .B(in_2[5]), .Less(1'b0), .Result(out_4[5]), .C_in(n1b_alu_5_c_out), .in_2(in_1[1:0]),
    .C_out(n1b_alu_6_c_out), .B_invert(in_1[2]), .A_invert(in_1[3]));  // open: Set, Overflow
  _1b_ALU u_1b_alu_7 (
    .A(in_3[6]), .B(in_2[6]), .Less(1'b0), .Result(out_4[6]), .C_in(n1b_alu_6_c_out), .in_2(in_1[1:0]),
    .C_out(n1b_alu_7_c_out), .B_invert(in_1[2]), .A_invert(in_1[3]));  // open: Set, Overflow
  _1b_ALU u_1b_alu_8 (
    .A(in_3[7]), .B(in_2[7]), .Less(1'b0), .Result(out_4[7]), .Set(n1b_alu_8_set), .Overflow(Overflow),
    .C_in(n1b_alu_7_c_out), .in_2(in_1[1:0]), .B_invert(in_1[2]), .A_invert(in_1[3]));  // open: C_out
  xor xor_1 (xor_1_out, n1b_alu_8_set, Overflow);
  Hex_Digit_Display hex_digit_display_6 (.value(out_4[7:4]));  // open: dp
  nor nor_1 (Zero, out_4[0], out_4[1], out_4[2], out_4[3], out_4[4], out_4[5], out_4[6], out_4[7]);
  Hex_Digit_Display hex_digit_display_7 (.value(out_4[3:0]));  // open: dp

  // Notes on the sheet:
  //   Input B
  //   Input A
endmodule
