// Logisim project project2.circ as structural Verilog: 2 circuits, main circuit Multiplication
module Multiplication (
  input  [7:0] Multiplicand,
  input  [7:0] Multiplier,
  output [7:0] HI,
  output [7:0] LO
);

  wire adder_1_cout, and_1_out, CLOCK_out, comparator_1_eq, d_ff_2_q, not_1_out, RESET_out;
  wire [0:0] Falling_q;
  wire [3:0] counter_1_q;
  wire [7:0] adder_1_out, multiplexer_1_out, multiplexer_2_out;
  wire [15:0] Rising_q;

  Button RESET (.out(RESET_out));
  Button CLOCK (.out(CLOCK_out));
  LED FINISHED (.in(comparator_1_eq));
  not not_1 (not_1_out, comparator_1_eq);
  Hex_Digit_Display hex_digit_display_1 (.value(Multiplicand[3:0]));  // open: dp
  Hex_Digit_Display hex_digit_display_2 (.value(Multiplicand[7:4]));  // open: dp
  Multiplexer #(.width(8)) multiplexer_1 (
    .in0({8{1'b0}}), .in1(Multiplicand), .out(multiplexer_1_out), .sel(multiplexer_2_out[0]));  // open: en
  and and_1 (and_1_out, CLOCK_out, not_1_out);
  Adder adder_1 (.a(multiplexer_1_out), .b(HI), .out(adder_1_out), .cin(1'b0), .cout(adder_1_cout));
  D_Flip_Flop d_ff_1 (.clk(and_1_out), .D(adder_1_cout), .Q(HI[7]), .reset(RESET_out));  // open: Qn, preset, en
  Counter #(.width(4), .max('hf), .ongoal("load")) counter_1 (
    .Q(counter_1_q), .clk(and_1_out), .clr(RESET_out));  // open: load, D, count, carry
  Register #(.width(16)) Rising (
    .D({adder_1_out, multiplexer_2_out}), .Q(Rising_q), .clk(and_1_out), .clr(RESET_out));  // open: en
  Hex_Digit_Display hex_digit_display_3 (.value(Multiplier[7:4]));  // open: dp
  Multiplexer #(.width(8)) multiplexer_2 (
    .in0(LO), .in1(Multiplier), .out(multiplexer_2_out), .sel(d_ff_2_q));  // open: en
  Register #(.width(16), .trigger("falling")) Falling (
    .D(Rising_q), .Q({HI[6:0], LO, Falling_q[0]}), .clk(and_1_out), .clr(RESET_out));  // open: en
  Comparator #(.width(4)) comparator_1 (.a(counter_1_q), .b(4'b1000), .eq(comparator_1_eq));  // open: gt, lt
  Hex_Digit_Display hex_digit_display_4 (.value(Multiplier[3:0]));  // open: dp
  Hex_Digit_Display hex_digit_display_5 (.value(HI[7:4]));  // open: dp
  D_Flip_Flop d_ff_2 (.clk(and_1_out), .D(1'b0), .Q(d_ff_2_q), .preset(RESET_out));  // open: Qn, en, reset
  Hex_Digit_Display hex_digit_display_6 (.value(HI[3:0]));  // open: dp
  Hex_Digit_Display hex_digit_display_7 (.value(LO[3:0]));  // open: dp
  Hex_Digit_Display hex_digit_display_8 (.value(LO[7:4]));  // open: dp

  // Notes on the sheet:
  //   MULTIPLICATION CIRCUIT
  //   2. Press the RESET button
  //   1. Enter binary values for multiplier and multiplicand
  //   3. Press clock repeatedly until LED Finished is ON
endmodule

module Division (
  input  [7:0] Dividend,
  input  [7:0] Divisor,
  output [7:0] Quotient,
  output [7:0] Remainder
);

  wire and_1_out, and_2_out, CLOCK_out, comparator_1_gt, comparator_2_eq, comparator_3_eq, d_ff_1_q,
       not_1_out, not_2_out, RESET_out, subtractor_1_bout;
  wire [0:0] multiplexer_3_out;
  wire [3:0] counter_1_q;
  wire [7:0] Falling_q, subtractor_1_out;
  wire [15:0] Falling_q_2, Rising_q;

  Button CLOCK (.out(CLOCK_out));
  LED FINISHED (.in(comparator_2_eq));
  not not_1 (not_1_out, comparator_2_eq);
  Button RESET (.out(RESET_out));
  and and_1 (and_1_out, CLOCK_out, not_1_out);
  Hex_Digit_Display hex_digit_display_1 (.value(Dividend[3:0]));  // open: dp
  Hex_Digit_Display hex_digit_display_2 (.value(Dividend[7:4]));  // open: dp
  Subtractor subtractor_1 (.a(Falling_q), .b(Divisor), .out(subtractor_1_out), .bout(subtractor_1_bout));  // open: bin
  Multiplexer #(.width(8)) multiplexer_1 (
    .in0(Falling_q), .in1(subtractor_1_out), .out(Quotient), .sel(and_2_out));  // open: en
  Comparator comparator_1 (.a(subtractor_1_out), .b({8{1'b1}}), .gt(comparator_1_gt));  // open: eq, lt
  Register #(.width(16)) Rising (
    .D({Quotient, Remainder}), .Q(Rising_q), .clk(and_1_out), .clr(RESET_out));  // open: en
  and and_2 (and_2_out, comparator_1_gt, not_2_out);
  not not_2 (not_2_out, subtractor_1_bout);
  Counter #(.width(4), .max('hf), .ongoal("load")) counter_1 (
    .Q(counter_1_q), .clk(and_1_out), .clr(RESET_out));  // open: load, D, count, carry
  Multiplexer #(.width(8)) multiplexer_2 (
    .in0({Falling_q_2[6:0], multiplexer_3_out[0]}), .in1(Dividend), .out(Remainder), .sel(d_ff_1_q));  // open: en
  Register #(.width(16), .trigger("falling")) Falling (
    .D(Rising_q), .Q({Falling_q_2[15], Falling_q, Falling_q_2[6:0]}), .clk(and_1_out), .clr(RESET_out));  // open: en
  Multiplexer multiplexer_3 (
    .in0(and_2_out), .in1(1'b0), .out(multiplexer_3_out[0]), .sel(comparator_3_eq));  // open: en
  Comparator #(.width(4)) comparator_2 (.a(counter_1_q), .b(4'b1000), .eq(comparator_2_eq));  // open: gt, lt
  Hex_Digit_Display hex_digit_display_3 (.value(Divisor[7:4]));  // open: dp
  Comparator comparator_3 (.a(Divisor), .b({8{1'b0}}), .eq(comparator_3_eq));  // open: gt, lt
  Hex_Digit_Display hex_digit_display_4 (.value(Divisor[3:0]));  // open: dp
  Hex_Digit_Display hex_digit_display_5 (.value(Quotient[7:4]));  // open: dp
  D_Flip_Flop d_ff_1 (.clk(and_1_out), .D(1'b0), .Q(d_ff_1_q), .preset(RESET_out));  // open: Qn, en, reset
  Hex_Digit_Display hex_digit_display_6 (.value(Quotient[3:0]));  // open: dp
  Hex_Digit_Display hex_digit_display_7 (.value(Remainder[3:0]));  // open: dp
  Hex_Digit_Display hex_digit_display_8 (.value(Remainder[7:4]));  // open: dp

  // Notes on the sheet:
  //   SEQUENTIAL DIVISION CIRCUIT
  //   2. Press the RESET button
  //   1. Enter binary values for dividend and divisor
  //   3. Press clock repeatedly until LED Finished is ON
endmodule
